// Logisim project inc.circ as structural Verilog: 2 circuits, main circuit main
module main (
  input  DIN,
  input  in_2,
  output DOUT_VLD,
  output [7:0] DOUT
);

  wire and_1_out, and_2_out, and_3_out, and_4_out, and_5_out, and_6_out, clock_1_out, clock_2_out,
       clock_3_out, clock_4_out, clock_5_out, clock_6_out, clock_7_out, clock_8_out, clock_9_out,
       clock_10_out, clock_11_out, clock_12_out, clock_13_out, clock_14_out, clock_15_out, clock_16_out,
       clock_17_out, clock_18_out, clock_19_out, clock_20_out, clock_21_out, clock_22_out, counter_2_carry,
       counter_3_carry, counter_4_carry, demultiplexer_1_out0, demultiplexer_1_out1, demultiplexer_1_out2,
       demultiplexer_1_out3, demultiplexer_1_out4, demultiplexer_1_out5, demultiplexer_1_out6,
       demultiplexer_1_out7, demultiplexer_2_out0, demultiplexer_2_out1, demultiplexer_2_out2,
       demultiplexer_2_out3, demultiplexer_2_out4, demultiplexer_2_out5, demultiplexer_2_out6,
       demultiplexer_2_out7, fsm_1_read, fsm_1_wait_first, fsm_1_wait_offset, fsm_1_wait_start, fsm_2_read,
       fsm_2_wait_first, fsm_2_wait_offset, fsm_2_wait_start, j_k_ff_1_q, j_k_ff_2_q, or_1_out, or_2_out,
       or_3_out, or_4_out, undriven;
  wire [2:0] counter_3_q, counter_4_q;
  wire [3:0] counter_1_q;
  wire [7:0] j_k_ff_3_q;

  Counter #(.max('hf), .width(4)) counter_1 (
    .clr(and_1_out), .up(1'b1), .count(or_1_out), .clk(clock_1_out), .Q(counter_1_q));  // open: load, D, carry
  Clock clock_1 (.out(clock_1_out));
  Clock clock_2 (.out(clock_2_out));
  Counter #(.max('hf), .width(4)) counter_2 (
    .load(1'b0), .up(1'b1), .count(or_3_out), .clk(clock_2_out), .carry(counter_2_carry));  // open: clr, D, Q
  FSM fsm_1 (
    .DIN(DIN), .READ_DONE(or_2_out), .WAIT_DONE(counter_4_carry), .WAIT_START(fsm_1_wait_start),
    .WAIT_OFFSET(fsm_1_wait_offset), .WAIT_FIRST(fsm_1_wait_first), .READ(fsm_1_read), .DATA_VALID(DOUT_VLD));  // open: WAIT_END
  FSM fsm_2 (
    .DIN(in_2), .READ_DONE(counter_3_carry), .WAIT_DONE(counter_2_carry), .WAIT_START(fsm_2_wait_start),
    .WAIT_OFFSET(fsm_2_wait_offset), .WAIT_FIRST(fsm_2_wait_first), .READ(fsm_2_read));  // open: WAIT_END, DATA_VALID
  or or_1 (or_1_out, fsm_1_wait_offset, fsm_1_wait_first, fsm_1_read);
  and and_1 (and_1_out, fsm_1_wait_offset, and_2_out);
  and and_2 (and_2_out, counter_1_q[0], counter_1_q[1], counter_1_q[2]);
  and and_3 (and_3_out, counter_1_q[0], counter_1_q[1], counter_1_q[2], counter_1_q[3]);
  or or_2 (or_2_out, and_3_out, and_1_out);
  Clock clock_3 (.out(clock_3_out));
  or or_3 (or_3_out, fsm_2_wait_first, fsm_2_read);
  and and_4 (and_4_out, in_2, counter_2_carry);
  Counter #(.max('h7), .width(3)) counter_3 (
    .clr(undriven), .load(1'b0), .up(1'b1), .count(or_4_out), .clk(clock_4_out), .carry(counter_3_carry),
    .Q(counter_3_q));  // open: D
  or or_4 (or_4_out, fsm_2_wait_offset, counter_2_carry);
  Clock clock_4 (.out(clock_4_out));
  and and_5 (and_5_out, DIN, and_3_out);
  Counter #(.max('h7), .width(3)) counter_4 (
    .up(1'b1), .count(and_6_out), .clk(clock_5_out), .carry(counter_4_carry), .Q(counter_4_q));  // open: clr, load, D
  and and_6 (and_6_out, fsm_1_read, and_3_out, j_k_ff_2_q);
  Clock clock_5 (.out(clock_5_out));
  J_K_Flip_Flop #(.trigger("falling")) j_k_ff_1 (
    .J(and_3_out), .K(1'b0), .clk(clock_3_out), .Q(j_k_ff_1_q), .reset(counter_4_carry));  // open: Qn, preset
  J_K_Flip_Flop #(.trigger("falling")) j_k_ff_2 (
    .J(j_k_ff_1_q), .K(1'b0), .clk(clock_6_out), .Q(j_k_ff_2_q), .reset(counter_4_carry));  // open: Qn, preset
  Clock clock_6 (.out(clock_6_out));
  Demultiplexer #(.select(3)) demultiplexer_1 (
    .out0(demultiplexer_1_out0), .out1(demultiplexer_1_out1), .out2(demultiplexer_1_out2),
    .out3(demultiplexer_1_out3), .out4(demultiplexer_1_out4), .out5(demultiplexer_1_out5),
    .out6(demultiplexer_1_out6), .out7(demultiplexer_1_out7), .in(and_4_out), .sel(counter_3_q));
  Demultiplexer #(.select(3)) demultiplexer_2 (
    .out0(demultiplexer_2_out0), .out1(demultiplexer_2_out1), .out2(demultiplexer_2_out2),
    .out3(demultiplexer_2_out3), .out4(demultiplexer_2_out4), .out5(demultiplexer_2_out5),
    .out6(demultiplexer_2_out6), .out7(demultiplexer_2_out7), .in(and_5_out), .sel(counter_4_q));
  J_K_Flip_Flop j_k_ff_3 (
    .J(demultiplexer_1_out0), .K(fsm_2_wait_start), .clk(clock_7_out), .Q(j_k_ff_3_q[0]));  // open: Qn, preset, reset
  Clock clock_7 (.out(clock_7_out));
  J_K_Flip_Flop j_k_ff_4 (
    .J(demultiplexer_1_out1), .K(fsm_2_wait_start), .clk(clock_8_out), .Q(j_k_ff_3_q[1]));  // open: Qn, preset, reset
  Clock clock_8 (.out(clock_8_out));
  J_K_Flip_Flop j_k_ff_5 (
    .J(demultiplexer_1_out2), .K(fsm_2_wait_start), .clk(clock_9_out), .Q(j_k_ff_3_q[2]));  // open: Qn, preset, reset
  Clock clock_9 (.out(clock_9_out));
  J_K_Flip_Flop j_k_ff_6 (
    .J(demultiplexer_1_out3), .K(fsm_2_wait_start), .clk(clock_10_out), .Q(j_k_ff_3_q[3]));  // open: Qn, preset, reset
  Clock clock_10 (.out(clock_10_out));
  J_K_Flip_Flop j_k_ff_7 (
    .J(demultiplexer_1_out4), .K(fsm_2_wait_start), .clk(clock_11_out), .Q(j_k_ff_3_q[4]));  // open: Qn, preset, reset
  Clock clock_11 (.out(clock_11_out));
  J_K_Flip_Flop j_k_ff_8 (
    .J(demultiplexer_1_out5), .K(fsm_2_wait_start), .clk(clock_12_out), .Q(j_k_ff_3_q[5]));  // open: Qn, preset, reset
  Clock clock_12 (.out(clock_12_out));
  J_K_Flip_Flop j_k_ff_9 (
    .J(demultiplexer_1_out6), .K(fsm_2_wait_start), .clk(clock_13_out), .Q(j_k_ff_3_q[6]));  // open: Qn, preset, reset
  Clock clock_13 (.out(clock_13_out));
  J_K_Flip_Flop j_k_ff_10 (
    .J(demultiplexer_1_out7), .K(fsm_2_wait_start), .clk(clock_14_out), .Q(j_k_ff_3_q[7]));  // open: Qn, preset, reset
  Clock clock_14 (.out(clock_14_out));
  J_K_Flip_Flop j_k_ff_11 (
    .J(demultiplexer_2_out0), .K(fsm_1_wait_start), .clk(clock_15_out), .Q(DOUT[0]));  // open: Qn, preset, reset
  Clock clock_15 (.out(clock_15_out));
  J_K_Flip_Flop j_k_ff_12 (
    .J(demultiplexer_2_out1), .K(fsm_1_wait_start), .clk(clock_16_out), .Q(DOUT[1]));  // open: Qn, preset, reset
  Clock clock_16 (.out(clock_16_out));
  J_K_Flip_Flop j_k_ff_13 (
    .J(demultiplexer_2_out2), .K(fsm_1_wait_start), .clk(clock_17_out), .Q(DOUT[2]));  // open: Qn, preset, reset
  Clock clock_17 (.out(clock_17_out));
  J_K_Flip_Flop j_k_ff_14 (
    .J(demultiplexer_2_out3), .K(fsm_1_wait_start), .clk(clock_18_out), .Q(DOUT[3]));  // open: Qn, preset, reset
  Clock clock_18 (.out(clock_18_out));
  J_K_Flip_Flop j_k_ff_15 (
    .J(demultiplexer_2_out4), .K(fsm_1_wait_start), .clk(clock_19_out), .Q(DOUT[4]));  // open: Qn, preset, reset
  Clock clock_19 (.out(clock_19_out));
  J_K_Flip_Flop j_k_ff_16 (
    .J(demultiplexer_2_out5), .K(fsm_1_wait_start), .clk(clock_20_out), .Q(DOUT[5]));  // open: Qn, preset, reset
  Clock clock_20 (.out(clock_20_out));
  J_K_Flip_Flop j_k_ff_17 (
    .J(demultiplexer_2_out6), .K(fsm_1_wait_start), .clk(clock_21_out), .Q(DOUT[6]));  // open: Qn, preset, reset
  Clock clock_21 (.out(clock_21_out));
  J_K_Flip_Flop j_k_ff_18 (
    .J(demultiplexer_2_out7), .K(fsm_1_wait_start), .clk(clock_22_out), .Q(DOUT[7]));  // open: Qn, preset, reset
  Clock clock_22 (.out(clock_22_out));
endmodule

module FSM (
  input  DIN,
  input  READ_DONE,
  input  WAIT_DONE,
  output WAIT_START,
  output WAIT_OFFSET,
  output WAIT_FIRST,
  output READ,
  output WAIT_END,
  output DATA_VALID
);

  wire and_1_out, and_2_out, and_3_out, and_4_out, and_5_out, nor_1_out, shift_register_1_p2,
       shift_register_1_p3, shift_register_1_p4;

  and and_1 (and_1_out, ~DIN, WAIT_START);  // AND_Gate
  and and_2 (and_2_out, READ_DONE, WAIT_OFFSET);
  and and_3 (and_3_out, WAIT_DONE, WAIT_FIRST);
  and and_4 (and_4_out, READ_DONE, READ);
  and and_5 (and_5_out, DIN, WAIT_END);
  // Shift_Register #(.length(6)) shift_register_1: pin names not known; wires that end beside it: 1'b0, shift_register_1_p2, shift_register_1_p3, shift_register_1_p4, WAIT_START, WAIT_OFFSET, WAIT_FIRST, READ, WAIT_END
  or or_1 (shift_register_1_p2, and_1_out, and_2_out, and_3_out, and_4_out, and_5_out, shift_register_1_p4);
  Clock clock_1 (.out(shift_register_1_p3));
  or or_2 (shift_register_1_p4, nor_1_out, DATA_VALID);
  nor nor_1 (nor_1_out, WAIT_START, WAIT_OFFSET, WAIT_FIRST, READ, WAIT_END, DATA_VALID);
endmodule
